# Fritzing sketch TP IoT (saved by Fritzing 0.9.2b)

parts:
  Part1 = Arduino Uno (Rev3)
  Raspberry_Pi_B_rev1 = Raspberry Pi B rev1
  LED1 = LED - 5mm [color="Red (633nm)" package="5 mm [THT]"]
  RHT1 = Humidity and Temperature Sensor RHT03
  J1 = female pin header, 2 pins [form="♀ (female)"]  # not connected
  J2 = female pin header, 2 pins [form="♀ (female)"]  # not connected
  LED3 = LED - 5mm [color="Red (633nm)" package="5 mm [THT]"]
  RHT2 = Humidity and Temperature Sensor RHT03
  J3 = female pin header, 2 pins [form="♀ (female)"]  # not connected
  LED4 = LED - 5mm [color="Red (633nm)" package="5 mm [THT]"]
  RHT3 = Humidity and Temperature Sensor RHT03
  J4 = female pin header, 2 pins [form="♀ (female)"]  # not connected
  J6 = female pin header, 2 pins [form="♀ (female)"]  # not connected
  Raspberry_Pi1 = Raspberry Pi 2

nets:
  N1: Part1.D13/SCK, LED3.anode
  N2: Part1.GND, LED3.cathode, RHT2.GND_1, RHT2.GND_2
  N3: Part1.D5_PWM, RHT2.Data-signal
  5V: Part1.5V, RHT2.Vcc
  N4: Raspberry_Pi_B_rev1.GND, LED1.cathode, RHT1.GND_1, RHT1.GND_2
  N5: Raspberry_Pi_B_rev1.GPIO_22, RHT1.Data-signal
  N6: Raspberry_Pi_B_rev1.GPIO_25, LED1.anode
  N7: Raspberry_Pi_B_rev1.GPIO_8, RHT1.Vcc
  N8: LED4.cathode, RHT3.GND_1, RHT3.GND_2, Raspberry_Pi1.GND, Raspberry_Pi1.GPIO27, Raspberry_Pi1.GPIO10, Raspberry_Pi1.GPIO15
  N9: LED4.anode, Raspberry_Pi1.GPIO9, Raspberry_Pi1.GPIO25
  N10: RHT3.Vcc, Raspberry_Pi1.GPIO11, Raspberry_Pi1.GPIO8
  N11: RHT3.Data-signal, Raspberry_Pi1.GPIO22, Raspberry_Pi1.GPIO23
  3V3: Raspberry_Pi1.3v3, Raspberry_Pi1.5V
  N12: Raspberry_Pi1.GPIO4, Raspberry_Pi1.GPIO14

notes:
  Long Pin
  Short Pin
  YwRobot Light Sensor
  AM2302 Temperature Sensor
  L-934ID-5V LED With
  +
  Out
  --
  Built-In Resistor
  AOUT
  DOUT
  GND
  VCC
