# Fritzing sketch TP IoT (saved by Fritzing 0.9.2b)

parts:
  Part1 = Arduino Uno (Rev3)
  Raspberry_Pi_B_rev1 = Raspberry Pi B rev1
  LED1 = LED - 5mm [color="Red (633nm)" package="5 mm [THT]"]
  RHT1 = Humidity and Temperature Sensor RHT03
  J1 = female pin header, 2 pins [form="♀ (female)"]  # not connected
  J2 = female pin header, 2 pins [form="♀ (female)"]  # not connected
  LED3 = LED - 5mm [color="Red (633nm)" package="5 mm [THT]"]
  RHT2 = Humidity and Temperature Sensor RHT03
  J3 = female pin header, 2 pins [form="♀ (female)"]  # not connected

nets:
  N1: Part1.D13/SCK, LED3.anode
  N2: Part1.GND, LED3.cathode, RHT2.GND_1, RHT2.GND_2
  N3: Part1.D5_PWM, RHT2.Data-signal
  5V: Part1.5V, RHT2.Vcc
  N4: Raspberry_Pi_B_rev1.GND, LED1.cathode, RHT1.GND_1, RHT1.GND_2
  N5: Raspberry_Pi_B_rev1.GPIO_22, RHT1.Data-signal
  N6: Raspberry_Pi_B_rev1.GPIO_25, LED1.anode
  N7: Raspberry_Pi_B_rev1.GPIO_8, RHT1.Vcc

notes:
  Long Pin
  Short Pin
  YwRobot Light Sensor
  AM2302 Temperature Sensor
  L-934ID-5V LED With
  +
  Out
  --
  Built-In Resistor
  AOUT
  DOUT
